# Fritzing sketch Diagram (saved by Fritzing 0.9.3b)
breadboards: 1

parts:
  MCU1 = Raspberry Pi Zero
  R1 = Resistor [tolerance=±5% resistance=220 package="0805 [SMD]"]
  R2 = Resistor [tolerance=±5% resistance=220 package="0805 [SMD]"]
  R3 = Resistor [tolerance=±5% resistance=1k package="2010 [SMD]"]
  R4 = Resistor [tolerance=±5% resistance=1k package="2010 [SMD]"]
  LED1 = smd LED [color="Red (633nm)" package="0805 [SMD]"]
  LED2 = smd LED [color="Green (555nm)" package="0603 [SMD]"]
  R5 = Resistor [tolerance=±5% resistance=1k package="2010 [SMD]"]
  HC-SR04_Sensor_1 = HC-SR04 Ultrasonic Distance Sensor
  J2 = Piezo Speaker

nets:
  N1: MCU1.pin_2, MCU1.pin_4, HC-SR04_Sensor_1.VCC
  N2: MCU1.pin_29, J2.pin2
  N3: MCU1.pin_31, R1.Pin_0
  N4: MCU1.pin_33, R2.Pin_0
  N5: MCU1.pin_34, MCU1.pin_39, LED1.cathode, LED2.cathode, HC-SR04_Sensor_1.GND, J2.pin1
  N6: MCU1.pin_35, HC-SR04_Sensor_1.TRIG
  N7: MCU1.pin_37, R3.Pin_0, R4.Pin_1
  N8: R1.Pin_1, LED1.anode
  N9: R2.Pin_1, LED2.anode
  N10: R3.Pin_1, HC-SR04_Sensor_1.ECHO
  N11: R4.Pin_0, R5.Pin_1
